# Fritzing sketch hemostasis-circuitdiagram (saved by Fritzing 1.0.3b)
breadboards: 1

parts:
  R1 = Resistor [tolerance=±5% power=0.25W resistance=100 package=THT]
  M1 = Arduino NANO RP2040 CONNECT with headers
  J1 = Piezo Speaker
  LED1 = LED - 5mm [color="Blue (430nm)" current=0.030A package="5 mm [THT]"]  # not connected
  R2 = Basic Force Sensing Resistor (FSR) [package=THT]  # not connected
  R3 = Resistor [tolerance=±5% power=0.25W resistance=10k package=THT]  # not connected
  S1 = Taiway 100-SP-X-T1 SPDT Miniature Toggle Switch [part_number=100-SP-X-T1-0-0-B1-M1 package=THT]
  U1 = mystery part, 8 pins [chip_label=USB-C]

nets:
  N1: R1.Pin_0, M1.VIN
  N2: M1.GND-4, M1.GND-29, U1.pin1
  N3: M1.D11, J1.pin1
  N4: S1.L2, U1.pin8
